# Fritzing sketch Untitled Sketch 4 (saved by Fritzing 0.9.3b)

parts:
  MH-ET_LIVE_ESP32_DEVKIT1 = MH-ET LIVE ESP32 DEVKIT 38 pins
  Part1 = OLED Monochrome 128x32 I2C [part_number=931]
  Part2 = Adafruit I2S Mic - SPH0645 [part_number="Adafruit #3421"]

nets:
  3V3: MH-ET_LIVE_ESP32_DEVKIT1.3V3, Part2.VDD
  N1: MH-ET_LIVE_ESP32_DEVKIT1.IO35, MH-ET_LIVE_ESP32_DEVKIT1.IO32, Part1.SCL
  N2: MH-ET_LIVE_ESP32_DEVKIT1.IO33, Part1.SDA
  N3: MH-ET_LIVE_ESP32_DEVKIT1.IO25, MH-ET_LIVE_ESP32_DEVKIT1.IO26, Part2.BCLK
  5V: MH-ET_LIVE_ESP32_DEVKIT1.5V, Part1.VIN
  GND: MH-ET_LIVE_ESP32_DEVKIT1.GND, Part1.GND, Part2.GND, Part2.SELECT
  N4: MH-ET_LIVE_ESP32_DEVKIT1.IO23, MH-ET_LIVE_ESP32_DEVKIT1.IO22, Part2.WS
  N5: MH-ET_LIVE_ESP32_DEVKIT1.RXD0, MH-ET_LIVE_ESP32_DEVKIT1.IO21, Part2.DATA

notes:
  Dispaly:
  SDA - IO33
  SCL - IO32
  VDD - 3.3V**
  VIN - 5V
  SPH0645:
  SEL - GND
  LRCL - IO22
  DOUT - IO21
  BCLK - io26
  VDD - 3.3V

custom parts:
  MH-ET LIVE ESP32 DEVKIT 38 pins: http://mh.nodebb.com/topic/2/mh-et-live-esp32-devkit
  OLED Monochrome 128x32 I2C: These displays are small, only about 1" diagonal, but very readable due to the high contrast of an OLED display. This display is made of 128x32 individual white OLED pixels, each one is turned on or off by the controller chip. Because the display makes its own light, no backlight is required. This reduces the power required to run the OLED and is why the display has such high contrast; we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
  Adafruit I2S Mic - SPH0645: For many microcontrollers, adding audio input is easy with one of our analog microphone breakouts. But as you get to bigger and better microcontrollers and microcomputers, you'll find that you don't always have an analog input, or maybe you want to avoid the noise that can seep in with an analog mic system. Once you get past 8-bit micros, you will often find an I2S peripheral, that can take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
